# Fritzing sketch AMRAS (saved by Fritzing 0.9.9b)
breadboards: 1

parts:
  Raspberry_Pi_1 = Raspberry Pi 3 [part_number=RPI-3-V1.2]
  J1 = Basic Servo
  J2 = Basic Servo
  PWM1 = PCA9685 16x12-bit PWM Breakout
  U1 = TCM8240MD [package=tcm8240md]
  U2 = Module 4 Relais 5V [package="Module 4 Relais 5V"]
  Power_plug1 = Power plug
  U3 = Transformer [package=transformer]
  U4 = Transformer [package=transformer]
  U5 = Transformer [package=transformer]
  U6 = Transformer [package=transformer]
  S1 = Toggle Switch [package=THT]
  S2 = Toggle Switch [package=THT]
  S3 = Toggle Switch [package=THT]

nets:
  N1: Raspberry_Pi_1.3v3, PWM1.no_name_yet#505
  N2: Raspberry_Pi_1.GPIO2, PWM1.no_name_yet#504
  N3: Raspberry_Pi_1.GPIO3, PWM1.no_name_yet#503
  N4: Raspberry_Pi_1.GPIO27, U2.IN4
  N5: Raspberry_Pi_1.GPIO22, U2.IN3
  N6: Raspberry_Pi_1.GPIO24, U2.IN1
  N7: Raspberry_Pi_1.GPIO23, U2.IN2
  GND: Raspberry_Pi_1.GND, PWM1.no_name_yet#501, PWM1.no_name_yet#601, PWM1.no_name_yet#701, PWM1.no_name_yet#1000, PWM1.no_name_yet#1001, U2.GND, Power_plug1.GND, U3.4, U4.4, U5.4, U6.4
  N8: J1.pulse, PWM1.no_name_yet#0
  N9: J2.pulse, PWM1.no_name_yet#1
  N10: PWM1.no_name_yet#100, PWM1.no_name_yet#101, PWM1.no_name_yet#606, PWM1.no_name_yet#706, U2.VCC, S2.COM
  N11: U1.GND, U1.PVDD(2.8V)
  N12: U2.K1-NF, U5.1
  N13: U2.K2-NF, U6.1
  N14: U2.K3-NF, U4.1
  N15: U2.K4-NF, U3.1
  N16: U2.K1-Com, U2.K2-Com, U2.K3-Com, U2.K4-Com, S3.COM
  N17: Power_plug1.VCC, S1.L2, S2.L2, S3.L2

custom parts:
  Module 4 Relais 5V: Module 4 Relais 5V 4x SPD-06VDC-SD-C
